// Logisim project s-mips.circ as structural Verilog
module S_MIPS_Board (
  input  DESHABILITAR_DISPATCHER,
  output halt
);

  wire button_1_out, CLK, CS, d_ff_1_q, LCLR, LoadRAM, LoadRAMOn, LW, R_R_W, R_W, ram_dispatcher_1_finished,
       RCS, Reset_out, RST, TTY_EN;
  wire [2:0] KDB;
  wire [3:0] LMask, Mask, ram_1_read_time, ram_1_write_time, RMask;
  wire [6:0] KDB_DATA, TTY_DATA;
  wire [15:0] Addr, LAddr, RAddr;
  wire [31:0] I0, I1, I2, I3, LData, ram_1_data_out_0, ram_1_data_out_1, ram_1_data_out_2, ram_1_data_out_3,
       RI0, RI1, RI2, RI3;

  TTY #(.rows(25), .cols(80)) tty_1 (.data(TTY_DATA), .clk(CLK), .we(TTY_EN), .clr(RST));
  not not_1 (LoadRAMOn, ram_dispatcher_1_finished);
  RAM_Dispatcher ram_dispatcher_1 (
    .WriteTime(ram_1_write_time), .Clock(CLK), .Data(LData), .Address(LAddr), .Mask(LMask),
    .Finished(ram_dispatcher_1_finished), .Write(LW), .CLR(LCLR));
  Keyboard #(.buflen(64)) keyboard_1 (.clk(CLK), .re(KDB[0]), .avail(KDB[2]), .data(KDB_DATA));  // open: clr
  RAM ram_1 (
    .Address(RAddr), .Data_Out_0(ram_1_data_out_0), .Data_Out_1(ram_1_data_out_1),
    .Data_Out_2(ram_1_data_out_2), .Data_Out_3(ram_1_data_out_3), .Data_In_0(RI0), .Data_In_1(RI1),
    .Data_In_2(RI2), .Data_In_3(RI3), .Mask(RMask), .nRead_Write(R_R_W), .Chip_Select(RCS),
    .Read_Time(ram_1_read_time), .Reset(button_1_out), .Write_Time(ram_1_write_time));
  Button button_1 (.out(button_1_out));
  D_Flip_Flop d_ff_1 (.clk(CLK), .D(1'b1), .Q(d_ff_1_q), .reset(Reset_out));  // open: Qn, preset, en
  Button Reset (.out(Reset_out));
  S_MIPS s_mips_1 (
    .Kbd_Enable(KDB[0]), .Address(Addr), .Kbd_Clear(KDB[1]), .Kbd_Available(KDB[2]), .RAM_In_0(I0),
    .Kbd_ASCII_Data(KDB_DATA), .RAM_In_1(I1), .TTY_Enable(TTY_EN), .RAM_In_2(I2), .RAM_In_3(I3),
    .TTY_ASCII_Data(TTY_DATA), .Reset(RST), .RAM_Out_0(ram_1_data_out_0), .Clock(CLK),
    .RAM_Out_1(ram_1_data_out_1), .Stop(halt), .RAM_Out_2(ram_1_data_out_2), .RAM_Out_3(ram_1_data_out_3),
    .Mask(Mask), .Read_Time(ram_1_read_time), .Write_Time(ram_1_write_time), .nRead_Write(R_W),
    .Chip_Select(CS));
  D_Flip_Flop d_ff_2 (.clk(CLK), .D(d_ff_1_q), .Qn(LCLR), .reset(Reset_out));  // open: Q, preset, en
  or or_1 (RST, LCLR, LoadRAM);
  Clock clock_1 (.out(CLK));
  Multiplexer #(.width(32), .enable("false")) multiplexer_1 (.in0(I0), .in1(LData), .out(RI0), .sel(LoadRAM));
  Multiplexer #(.width(32), .enable("false")) multiplexer_2 (.in0(I1), .in1(LData), .out(RI1), .sel(LoadRAM));
  Multiplexer #(.width(32), .enable("false")) multiplexer_3 (.in0(I2), .in1(LData), .out(RI2), .sel(LoadRAM));
  Multiplexer #(.width(32), .enable("false")) multiplexer_4 (.in0(I3), .in1(LData), .out(RI3), .sel(LoadRAM));
  and and_1 (LoadRAM, ~DESHABILITAR_DISPATCHER, LoadRAMOn);  // AND_Gate
  Multiplexer #(.width(16), .enable("false")) multiplexer_5 (.in0(Addr), .in1(LAddr), .out(RAddr), .sel(LoadRAM));
  Multiplexer #(.width(4), .enable("false")) multiplexer_6 (.in0(Mask), .in1(LMask), .out(RMask), .sel(LoadRAM));
  Multiplexer #(.enable("false")) multiplexer_7 (.in0(CS), .in1(LW), .out(RCS), .sel(LoadRAM));
  Multiplexer #(.enable("false")) multiplexer_8 (.in0(R_W), .in1(LW), .out(R_R_W), .sel(LoadRAM));

  // Notes on the sheet:
  //   NO MODIFICAR
  //   Keyboard
endmodule

module RAM (
  input  [15:0] Address,
  input  [31:0] Data_In_0,
  input  [31:0] Data_In_1,
  input  [31:0] Data_In_2,
  input  [31:0] Data_In_3,
  input  [3:0] Mask,
  input  nRead_Write,
  input  Chip_Select,
  input  Reset,
  output [31:0] Data_Out_0,
  output [31:0] Data_Out_1,
  output [31:0] Data_Out_2,
  output [31:0] Data_Out_3,
  output [3:0] Read_Time,
  output [3:0] Write_Time
);

  wire and_2_out, and_3_out, and_4_out, and_5_out, and_6_out, and_7_out, and_8_out, and_9_out, Changed, CLK,
       comparator_2_eq, comparator_3_eq, comparator_4_eq, comparator_5_eq, comparator_6_eq, Count,
       demultiplexer_3_out0, Idle, Idle_q, Load, Load0, Load1, nand_1_out, or_1_out, or_2_out, or_3_out,
       or_4_out, or_5_out, or_6_out, or_7_out, or_8_out, or_9_out, or_10_out, Proc_q, Update_Mem, Zero_Time;
  wire [3:0] counter_1_q, multiplexer_1_out, subtractor_1_out;
  wire [31:0] register_1_q, register_2_q, register_3_q, register_4_q, register_5_q;

  // Probe on 4'b0011
  // Probe on 4'b0010
  Multiplexer #(.width(4), .enable("false")) multiplexer_1 (
    .in0(4'b0011), .in1(4'b0010), .out(multiplexer_1_out), .sel(nRead_Write));
  or or_1 (or_1_out, Idle, Update_Mem);
  or or_2 (or_2_out, ~Chip_Select, Reset);  // OR_Gate
  Subtractor #(.width(4)) subtractor_1 (.a(multiplexer_1_out), .b(4'b0010), .out(subtractor_1_out));  // open: bin, bout
  D_Flip_Flop u_Idle (.clk(CLK), .D(or_1_out), .Q(Idle_q), .preset(or_2_out));  // open: Qn, en, reset
  Demultiplexer #(.enable("false")) demultiplexer_1 (.out0(Idle), .out1(Load0), .in(Idle_q), .sel(Changed));
  // Probe on counter_1_q
  Counter #(.width(4), .max('hf)) counter_1 (
    .load(Load), .D(subtractor_1_out), .count(Count), .Q(counter_1_q), .clk(CLK), .clr(or_3_out));  // open: carry
  or or_3 (or_3_out, ~Chip_Select, Reset);  // OR_Gate
  Comparator #(.width(4), .mode("unsigned")) comparator_1 (
    .a(4'b0000), .b(counter_1_q), .eq(Zero_Time));  // open: gt, lt
  or or_4 (or_4_out, Count, Load0, Load1);
  Register #(.width(32)) register_1 (.D(Data_In_0), .en(Chip_Select), .Q(register_1_q), .clk(CLK), .clr(or_5_out));
  or or_5 (or_5_out, ~Chip_Select, Reset);  // OR_Gate
  Register #(.width(32)) register_2 (.D(Data_In_1), .en(Chip_Select), .Q(register_2_q), .clk(CLK), .clr(or_6_out));
  or or_6 (or_6_out, ~Chip_Select, Reset);  // OR_Gate
  Register #(.width(32)) register_3 (.D(Data_In_2), .en(Chip_Select), .Q(register_3_q), .clk(CLK), .clr(or_7_out));
  or or_7 (or_7_out, ~Chip_Select, Reset);  // OR_Gate
  Register #(.width(32)) register_4 (.D(Data_In_3), .en(Chip_Select), .Q(register_4_q), .clk(CLK), .clr(or_8_out));
  or or_8 (or_8_out, ~Chip_Select, Reset);  // OR_Gate
  Register #(.width(32)) register_5 (
    .D({{11{1'b1}}, nRead_Write, Mask, Address}), .en(Chip_Select), .Q(register_5_q), .clk(CLK),
    .clr(or_9_out));
  or or_9 (or_9_out, ~Chip_Select, Reset);  // OR_Gate
  D_Flip_Flop Proc (.clk(CLK), .D(or_4_out), .Q(Proc_q), .reset(or_10_out));  // open: Qn, preset, en
  or or_10 (or_10_out, ~Chip_Select, Reset);  // OR_Gate
  Demultiplexer #(.enable("false")) demultiplexer_2 (
    .out0(Count), .out1(Update_Mem), .in(demultiplexer_3_out0), .sel(Zero_Time));
  Demultiplexer #(.enable("false")) demultiplexer_3 (
    .out0(demultiplexer_3_out0), .out1(Load1), .in(Proc_q), .sel(Changed));
  Clock clock_1 (.out(CLK));
  Comparator #(.width(32)) comparator_2 (.a(register_1_q), .b(Data_In_0), .eq(comparator_2_eq));  // open: gt, lt
  Comparator #(.width(32)) comparator_3 (.a(register_2_q), .b(Data_In_1), .eq(comparator_3_eq));  // open: gt, lt
  Comparator #(.width(32)) comparator_4 (.a(register_3_q), .b(Data_In_2), .eq(comparator_4_eq));  // open: gt, lt
  Comparator #(.width(32)) comparator_5 (.a(register_4_q), .b(Data_In_3), .eq(comparator_5_eq));  // open: gt, lt
  Comparator #(.width(32)) comparator_6 (
    .a(register_5_q), .b({{11{1'b1}}, nRead_Write, Mask, Address}), .eq(comparator_6_eq));  // open: gt, lt
  nand nand_1 (nand_1_out, comparator_6_eq, comparator_2_eq, comparator_3_eq, comparator_4_eq, comparator_5_eq);
  and and_1 (Changed, nand_1_out, Chip_Select);
  or or_11 (Load, Count, Load1, Load0);
  and and_2 (and_2_out, Mask[0], Update_Mem, nRead_Write);
  and and_3 (and_3_out, Mask[1], Update_Mem, nRead_Write);
  and and_4 (and_4_out, Mask[2], Update_Mem, nRead_Write);
  and and_5 (and_5_out, Mask[3], Update_Mem, nRead_Write);
  RAM_part #(.addrWidth(16), .dataWidth(32), .bus("separate")) ram_1 (
    .addr(Address), .din(Data_In_0), .data(Data_Out_0), .str(and_2_out), .sel(Chip_Select), .clk(CLK),
    .ld(and_6_out), .clr(Reset));
  and and_6 (and_6_out, ~nRead_Write, Idle);  // AND_Gate
  RAM_part #(.addrWidth(16), .dataWidth(32), .bus("separate")) ram_2 (
    .addr(Address), .din(Data_In_1), .data(Data_Out_1), .str(and_3_out), .sel(Chip_Select), .clk(CLK),
    .ld(and_7_out), .clr(Reset));
  and and_7 (and_7_out, ~nRead_Write, Idle);  // AND_Gate
  RAM_part #(.addrWidth(16), .dataWidth(32), .bus("separate")) ram_3 (
    .addr(Address), .din(Data_In_2), .data(Data_Out_2), .str(and_4_out), .sel(Chip_Select), .clk(CLK),
    .ld(and_8_out), .clr(Reset));
  and and_8 (and_8_out, ~nRead_Write, Idle);  // AND_Gate
  RAM_part #(.addrWidth(16), .dataWidth(32), .bus("separate")) ram_4 (
    .addr(Address), .din(Data_In_3), .data(Data_Out_3), .str(and_5_out), .sel(Chip_Select), .clk(CLK),
    .ld(and_9_out), .clr(Reset));
  and and_9 (and_9_out, ~nRead_Write, Idle);  // AND_Gate

  assign Read_Time = 4'b0011;
  assign Write_Time = 4'b0010;

  // Other names for the same wires on the sheet: M0 = Mask[0]; M1 = Mask[1]; M2 = Mask[2]; M3 = Mask[3];
  //   RW = nRead_Write; CLR = Reset; CS = Chip_Select; Load2 = Count

  // Notes on the sheet:
  //   NO MODIFICAR
  //   excepto quizás los valores RT y WT
  //   BANK0
  //   BANK1
  //   BANK2
  //   BANK3
endmodule

module S_MIPS (
  input  Kbd_Available,
  input  [6:0] Kbd_ASCII_Data,
  input  [31:0] RAM_Out_0,
  input  [31:0] RAM_Out_1,
  input  Reset,
  input  [31:0] RAM_Out_2,
  input  Clock,
  input  [31:0] RAM_Out_3,
  input  [3:0] Read_Time,
  input  [3:0] Write_Time,
  output Kbd_Enable,
  output [15:0] Address,
  output Kbd_Clear,
  output TTY_Enable,
  output [6:0] TTY_ASCII_Data,
  output Stop,
  output [31:0] RAM_In_0,
  output [31:0] RAM_In_1,
  output [31:0] RAM_In_2,
  output [31:0] RAM_In_3,
  output [3:0] Mask,
  output nRead_Write,
  output Chip_Select
);


  // Other names for the same wires on the sheet: CLK = Clock; CLR = Reset; CS = Chip_Select;
  //   KBD_AVAIL = Kbd_Available; KBD_CLR = Kbd_Clear; KBD_DATA[6:0] = Kbd_ASCII_Data; RAM_A[15:0] = Address;
  //   RAM_INPUT_0[31:0] = RAM_In_0; RAM_INPUT_1[31:0] = RAM_In_1; RAM_INPUT_2[31:0] = RAM_In_2;
  //   RAM_INPUT_3[31:0] = RAM_In_3; RAM_MASK[3:0] = Mask; RAM_OUTPUT_0[31:0] = RAM_Out_0;
  //   RAM_OUTPUT_1[31:0] = RAM_Out_1; RAM_OUTPUT_2[31:0] = RAM_Out_2; RAM_OUTPUT_3[31:0] = RAM_Out_3;
  //   RW = nRead_Write; TTY_DATA[6:0] = TTY_ASCII_Data

  // Notes on the sheet:
  //   RAM ADDRESS
  //   DATA FROM RAM
  //   DATA TO RAM
  //   DATA WRITE MASK
  //   RAM TIMING
  //   RAM CONTROL
  //   KEYBOARD
  //   TTY
  //   SEQUENCING
endmodule

module RAM_Dispatcher (
  input  [3:0] WriteTime,
  input  Clock,
  input  CLR,
  output [31:0] Data,
  output [15:0] Address,
  output [3:0] Mask,
  output Finished,
  output Write
);

  wire demultiplexer_2_out1, demultiplexer_3_out1, End, IDLE_q, IncAddr, Load, or_1_out, or_2_out, While_q,
       WriteEnd;
  wire [3:0] counter_1_q;
  wire [31:0] CurrentAddress_q;

  Counter #(.width(32), .max('hffffffff)) CurrentAddress (
    .count(IncAddr), .Q({CurrentAddress_q[31:18], Address, CurrentAddress_q[1:0]}), .clk(Clock), .clr(CLR));  // open: load, D, carry
  or or_1 (or_1_out, IncAddr, demultiplexer_3_out1, Finished);
  D_Flip_Flop IDLE (.clk(Clock), .D(or_1_out), .Q(IDLE_q), .preset(CLR));  // open: Qn, en, reset
  Demultiplexer #(.enable("false")) demultiplexer_1 (.out0(Load), .out1(Finished), .in(IDLE_q), .sel(End));
  D_Flip_Flop While (.clk(Clock), .D(or_2_out), .Q(While_q), .reset(CLR));  // open: Qn, preset, en
  or or_2 (or_2_out, Write, Load);
  RAM_part #(.addrWidth(18), .dataWidth(32)) ram_1 (
    .addr({Address, CurrentAddress_q[1:0]}), .data(Data), .clk(Clock));  // open: sel, ld, clr
  Demultiplexer #(.enable("false")) demultiplexer_2 (
    .out0(Write), .out1(demultiplexer_2_out1), .in(While_q), .sel(WriteEnd));
  Decoder #(.select(2)) decoder_1 (
    .out0(Mask[0]), .out1(Mask[1]), .out2(Mask[2]), .out3(Mask[3]), .sel(CurrentAddress_q[1:0]));  // open: en
  Demultiplexer #(.enable("false")) demultiplexer_3 (
    .out0(IncAddr), .out1(demultiplexer_3_out1), .in(demultiplexer_2_out1), .sel(End));
  Counter #(.width(4), .max('hf)) counter_1 (
    .load(Load), .D(WriteTime), .count(Write), .Q(counter_1_q), .clk(Clock));  // open: carry, clr
  Comparator #(.width(32)) comparator_1 (.a(Data), .b({32{1'b1}}), .eq(End));  // open: gt, lt
  Comparator #(.width(4)) comparator_2 (.a(4'b0000), .b(counter_1_q), .eq(WriteEnd));  // open: gt, lt

  // Other names for the same wires on the sheet: CLK = Clock; Count = Write; WT[3:0] = WriteTime
endmodule

module Register_File (
  input  [4:0] DA,
  input  [31:0] DI,
  input  R_W,
  input  [4:0] SA,
  input  [4:0] SB,
  input  Clk,
  input  Reset,
  input  Pop,
  input  Push,
  input  Random,
  input  KBD,
  input  Kbd_Available,
  input  [6:0] Kbd_ASCII_Data,
  output [31:0] A,
  output [31:0] B,
  output [31:0] SP
);

  wire and_1_out, and_2_out, comparator_1_eq, not_1_out, not_2_out, R0, R1, R2, R3, R4, R5, R6, R7, R8, R9,
       R10, R11, R12, R13, R14, R15, R16, R17, R18, R19, R20, R21, R22, R23, R24, R25, R26, R27, R28, R29,
       R30, R31;
  wire [1:0] Code;
  wire [31:0] adder_1_out, D0, D1, D2, D3, D4, D5, D6, D7, D8, D9, D10, D11, D12, D13, D14, D15, D16, D17,
       D18, D19, D20, D21, D22, D23, D24, D25, D26, D27, D28, D29, D30, datainput, Di_t, E31, KBD_DATA,
       multiplexer_2_out, multiplexer_4_out, random_1_out, subtractor_1_out;

  // Probe on SA
  // Probe on SB
  // Probe on DA
  // Probe on DI
  assign KBD_DATA = {{25{1'b0}}, Kbd_ASCII_Data};  // Bit_Extender bit_extender_1
  Decoder #(.select(5)) decoder_1 (
    .out0(R0), .out1(R1), .out2(R2), .out3(R3), .out4(R4), .out5(R5), .out6(R6), .out7(R7), .out8(R8),
    .out9(R9), .out10(R10), .out11(R11), .out12(R12), .out13(R13), .out14(R14), .out15(R15), .out16(R16),
    .out17(R17), .out18(R18), .out19(R19), .out20(R20), .out21(R21), .out22(R22), .out23(R23), .out24(R24),
    .out25(R25), .out26(R26), .out27(R27), .out28(R28), .out29(R29), .out30(R30), .out31(R31), .sel(DA),
    .en(R_W));
  and and_1 (and_1_out, KBD, Kbd_Available);
  and and_2 (and_2_out, KBD, ~Kbd_Available);  // AND_Gate
  Multiplexer #(.select(5), .width(32)) multiplexer_1 (
    .in0(D0), .in1(D1), .in2(D2), .in3(D3), .in4(D4), .in5(D5), .in6(D6), .in7(D7), .in8(D8), .in9(D9),
    .in10(D10), .in11(D11), .in12(D12), .in13(D13), .in14(D14), .in15(D15), .in16(D16), .in17(D17),
    .in18(D18), .in19(D19), .in20(D20), .in21(D21), .in22(D22), .in23(D23), .in24(D24), .in25(D25),
    .in26(D26), .in27(D27), .in28(D28), .in29(D29), .in30(D30), .in31(SP), .out(A), .sel(SA), .en(not_1_out));
  not not_1 (not_1_out, R_W);
  or or_1 (Code[0], Random, and_2_out);
  or or_2 (Code[1], and_1_out, and_2_out);
  Comparator #(.width(5), .mode("unsigned")) comparator_1 (
    .a(DA), .b({5{1'b1}}), .eq(comparator_1_eq));  // open: gt, lt
  Register #(.width(32)) u_R0 (.D(Di_t), .en(R0), .Q(D0), .clk(Clk), .clr(Reset));
  Register #(.width(32)) u_R4 (.D(Di_t), .en(R4), .Q(D4), .clk(Clk), .clr(Reset));
  Register #(.width(32)) u_R8 (.D(Di_t), .en(R8), .Q(D8), .clk(Clk), .clr(Reset));
  Register #(.width(32)) u_R12 (.D(Di_t), .en(R12), .Q(D12), .clk(Clk), .clr(Reset));
  Register #(.width(32)) u_R16 (.D(Di_t), .en(R16), .Q(D16), .clk(Clk), .clr(Reset));
  Register #(.width(32)) u_R20 (.D(Di_t), .en(R20), .Q(D20), .clk(Clk), .clr(Reset));
  Register #(.width(32)) u_R24 (.D(Di_t), .en(R24), .Q(D24), .clk(Clk), .clr(Reset));
  Register #(.width(32)) u_R28 (.D(Di_t), .en(R28), .Q(D28), .clk(Clk), .clr(Reset));
  Multiplexer #(.width(32), .enable("false")) multiplexer_2 (
    .in0(SP), .in1(datainput), .out(multiplexer_2_out), .sel(comparator_1_eq));
  Multiplexer #(.select(5), .width(32)) multiplexer_3 (
    .in0(D0), .in1(D1), .in2(D2), .in3(D3), .in4(D4), .in5(D5), .in6(D6), .in7(D7), .in8(D8), .in9(D9),
    .in10(D10), .in11(D11), .in12(D12), .in13(D13), .in14(D14), .in15(D15), .in16(D16), .in17(D17),
    .in18(D18), .in19(D19), .in20(D20), .in21(D21), .in22(D22), .in23(D23), .in24(D24), .in25(D25),
    .in26(D26), .in27(D27), .in28(D28), .in29(D29), .in30(D30), .in31(SP), .out(B), .sel(SB), .en(not_2_out));
  not not_2 (not_2_out, R_W);
  Subtractor #(.width(32)) subtractor_1 (.a(SP), .b(32'h4), .out(subtractor_1_out));  // open: bin, bout
  Adder #(.width(32)) adder_1 (.a(multiplexer_2_out), .b(32'h4), .out(adder_1_out));  // open: cin, cout
  Register #(.width(32)) u_R1 (.D(Di_t), .en(R1), .Q(D1), .clk(Clk), .clr(Reset));
  Register #(.width(32)) u_R5 (.D(Di_t), .en(R5), .Q(D5), .clk(Clk), .clr(Reset));
  Register #(.width(32)) u_R9 (.D(Di_t), .en(R9), .Q(D9), .clk(Clk), .clr(Reset));
  Register #(.width(32)) u_R13 (.D(Di_t), .en(R13), .Q(D13), .clk(Clk), .clr(Reset));
  Register #(.width(32)) u_R17 (.D(Di_t), .en(R17), .Q(D17), .clk(Clk), .clr(Reset));
  Register #(.width(32)) u_R21 (.D(Di_t), .en(R21), .Q(D21), .clk(Clk), .clr(Reset));
  Register #(.width(32)) u_R25 (.D(Di_t), .en(R25), .Q(D25), .clk(Clk), .clr(Reset));
  Register #(.width(32)) u_R29 (.D(Di_t), .en(R29), .Q(D29), .clk(Clk), .clr(Reset));
  // Probe on {32{1'b1}}
  Multiplexer #(.select(2), .width(32), .enable("false")) multiplexer_4 (
    .in0(datainput), .in1(subtractor_1_out), .in2(adder_1_out), .out(multiplexer_4_out), .sel({Pop, Push}));  // open: in3
  Register #(.width(32)) u_R2 (.D(Di_t), .en(R2), .Q(D2), .clk(Clk), .clr(Reset));
  Register #(.width(32)) u_R6 (.D(Di_t), .en(R6), .Q(D6), .clk(Clk), .clr(Reset));
  Register #(.width(32)) u_R10 (.D(Di_t), .en(R10), .Q(D10), .clk(Clk), .clr(Reset));
  Register #(.width(32)) u_R14 (.D(Di_t), .en(R14), .Q(D14), .clk(Clk), .clr(Reset));
  Register #(.width(32)) u_R18 (.D(Di_t), .en(R18), .Q(D18), .clk(Clk), .clr(Reset));
  Register #(.width(32)) u_R22 (.D(Di_t), .en(R22), .Q(D22), .clk(Clk), .clr(Reset));
  Register #(.width(32)) u_R26 (.D(Di_t), .en(R26), .Q(D26), .clk(Clk), .clr(Reset));
  Register #(.width(32)) u_R30 (.D(Di_t), .en(R30), .Q(D30), .clk(Clk), .clr(Reset));
  Random #(.width(32)) random_1 (.clk(Clk), .next(1'b1), .out(random_1_out));  // open: clr
  Register #(.width(32)) u_R3 (.D(Di_t), .en(R3), .Q(D3), .clk(Clk), .clr(Reset));
  Register #(.width(32)) u_R7 (.D(Di_t), .en(R7), .Q(D7), .clk(Clk), .clr(Reset));
  Register #(.width(32)) u_R11 (.D(Di_t), .en(R11), .Q(D11), .clk(Clk), .clr(Reset));
  Register #(.width(32)) u_R15 (.D(Di_t), .en(R15), .Q(D15), .clk(Clk), .clr(Reset));
  Register #(.width(32)) u_R19 (.D(Di_t), .en(R19), .Q(D19), .clk(Clk), .clr(Reset));
  Register #(.width(32)) u_R23 (.D(Di_t), .en(R23), .Q(D23), .clk(Clk), .clr(Reset));
  Register #(.width(32)) u_R27 (.D(Di_t), .en(R27), .Q(D27), .clk(Clk), .clr(Reset));
  Register #(.width(32)) u_R31 (.D(E31), .en(R31), .Q(SP), .clk(Clk), .clr(Reset));
  Multiplexer #(.select(2), .width(32), .disabled(0), .enable("false")) multiplexer_5 (
    .in0(DI), .in1(random_1_out), .in2(KBD_DATA), .in3({32{1'b1}}), .out(Di_t), .sel(Code));
  Multiplexer #(.width(32), .enable("false")) multiplexer_6 (
    .in0(multiplexer_4_out), .in1({32{1'b1}}), .out(E31), .sel(Reset));
  // Probe on A
  // Probe on B

  // Other names for the same wires on the sheet: D31[31:0] = SP; Data_A[31:0] = A; Data_B[31:0] = B;
  //   Data_In[31:0] = DI; KBD_AVAIL = Kbd_Available; Rnd = Random; RS = Reset

  // Notes on the sheet:
  //   Inputs
  //   Data Address
  //   Data In
  //   Read/Write
  //   Selector A
  //   Selector B
  //   Registers
  //   Outputs
  //   Data A
  //   Data B
endmodule

module ALU (
  input  [31:0] A,
  input  [31:0] B,
  input  [3:0] Operation,
  input  M_D,
  input  Push_Pop,
  input  [31:0] SP,
  output [31:0] R
);

  wire comparator_1_lt, comparator_2_lt;
  wire [3:0] divider_2_out;
  wire [31:0] add, \and , div, high, low, Mod, mod_t, mult, multiplexer_1_out, \nor , \or , Signed_Current,
       Signed_Div, Signed_Mult, slt, sltu, sub, Unsigned_Current, Unsigned_Div, Unsigned_Mult, \xor ;

  // Probe on A
  // Probe on B
  assign \and  = A & B;  // AND_Gate and_1, 32 bits wide
  assign \or  = A | B;  // OR_Gate or_1, 32 bits wide
  Adder #(.width(32)) adder_1 (.a(A), .b(B), .out(add));  // open: cin, cout
  Subtractor #(.width(32)) subtractor_1 (.a(A), .b(B), .out(sub));  // open: bin, bout
  Multiplier #(.width(32)) multiplier_1 (.a(A), .b(B), .out(mult));  // open: cin, cout
  Divider #(.width(32)) divider_1 (.a(A), .b(B), .out(div), .rem(mod_t));  // open: upper
  assign \nor  = ~(A | B);  // NOR_Gate nor_1, 32 bits wide
  assign \xor  = A ^ B;  // XOR_Gate xor_1, 32 bits wide
  Comparator #(.width(32)) comparator_1 (.a(A), .b(B), .lt(comparator_1_lt));  // open: gt, eq
  assign slt = {{31{1'b0}}, comparator_1_lt};  // Bit_Extender bit_extender_1
  Comparator #(.width(32), .mode("unsigned")) comparator_2 (.a(A), .b(B), .lt(comparator_2_lt));  // open: gt, eq
  assign sltu = {{31{1'b0}}, comparator_2_lt};  // Bit_Extender bit_extender_2
  Mult mult_1 (
    .A(A), .B(B), .Output(Unsigned_Mult), .Output_2(Signed_Mult), .Output_3(Unsigned_Current),
    .Output_4(Signed_Current));
  Div div_1 (.A(A), .B(B), .Mod(Mod), .Output(Unsigned_Div), .Output_2(Signed_Div));
  Divider #(.width(4)) divider_2 (.a(Operation), .b(4'b0010), .out(divider_2_out));  // open: upper, rem
  Multiplexer #(.select(4), .width(32)) multiplexer_1 (
    .in0(add), .in1(sub), .in2(Signed_Mult), .in3(Unsigned_Mult), .in4(Unsigned_Div), .in5(Signed_Div),
    .in6(\and ), .in7(\or ), .in8(\nor ), .in9(\xor ), .in10(slt), .in11(sltu), .out(multiplexer_1_out),
    .sel(Operation));  // open: in12, in13, in14, in15, en
  Multiplexer #(.select(2), .width(32), .enable("false")) multiplexer_2 (
    .in0(Unsigned_Current), .in1(Signed_Current), .in2(Mod), .in3(Mod), .out(high), .sel(divider_2_out[1:0]));
  // Probe on multiplexer_1_out
  Multiplexer #(.width(32)) multiplexer_3 (.in0(multiplexer_1_out), .in1(SP), .out(R), .sel(Push_Pop));  // open: en
  Register #(.width(32)) u_High (.D(high), .en(M_D));  // open: Q, clk, clr
  Register #(.width(32)) u_Low (.D(low), .en(M_D));  // open: Q, clk, clr

  // Other names for the same wires on the sheet: Op[3:0] = Operation
endmodule

module Mult (
  input  [31:0] A,
  input  [31:0] B,
  output [31:0] Output,
  output [31:0] Output_2,
  output [31:0] Output_3,
  output [31:0] Output_4
);

  wire [31:0] a_denied, b_denied, multiplexer_1_out, multiplexer_2_out, not_1_out, not_2_out;

  assign not_1_out = ~A;  // NOT_Gate not_1, 32 bits wide
  Adder #(.width(32)) adder_1 (.a(not_1_out), .b(32'h1), .out(a_denied));  // open: cin, cout
  assign not_2_out = ~B;  // NOT_Gate not_2, 32 bits wide
  Adder #(.width(32)) adder_2 (.a(not_2_out), .b(32'h1), .out(b_denied));  // open: cin, cout
  Multiplexer #(.width(32)) multiplexer_1 (.in0(A), .in1(a_denied), .out(multiplexer_1_out), .sel(A[31]));  // open: en
  Multiplexer #(.width(32)) multiplexer_2 (.in0(B), .in1(b_denied), .out(multiplexer_2_out), .sel(B[31]));  // open: en
  Multiplier #(.width(32)) multiplier_1 (.a(A), .b(B), .out(Output_2), .cin({32{1'b0}}), .cout(Output_4));
  Multiplier #(.width(32)) multiplier_2 (
    .a(multiplexer_1_out), .b(multiplexer_2_out), .out(Output), .cin({32{1'b0}}), .cout(Output_3));

  // Other names for the same wires on the sheet: a_sign = A[31]; b_sign = B[31]; Signed_current[31:0] = Output_4;
  //   Signed_multiply[31:0] = Output_2; Unsigned_current[31:0] = Output_3; Unsigned_multiply[31:0] = Output

  // Notes on the sheet:
  //   Negate Inputs
endmodule

module Div (
  input  [31:0] A,
  input  [31:0] B,
  output [31:0] Output,
  output [31:0] Mod,
  output [31:0] Output_2
);

  wire [31:0] a_denied, b_denied, multiplexer_1_out, multiplexer_2_out, not_1_out, not_2_out;

  assign not_1_out = ~A;  // NOT_Gate not_1, 32 bits wide
  Adder #(.width(32)) adder_1 (.a(not_1_out), .b(32'h1), .out(a_denied));  // open: cin, cout
  assign not_2_out = ~B;  // NOT_Gate not_2, 32 bits wide
  Adder #(.width(32)) adder_2 (.a(not_2_out), .b(32'h1), .out(b_denied));  // open: cin, cout
  Multiplexer #(.width(32)) multiplexer_1 (.in0(A), .in1(a_denied), .out(multiplexer_1_out), .sel(A[31]));  // open: en
  Multiplexer #(.width(32)) multiplexer_2 (.in0(B), .in1(b_denied), .out(multiplexer_2_out), .sel(B[31]));  // open: en
  Divider #(.width(32)) divider_1 (.a(A), .b(B), .out(Output_2), .upper({32{1'b0}}));  // open: rem
  Divider #(.width(32)) divider_2 (
    .a(multiplexer_1_out), .b(multiplexer_2_out), .out(Output), .upper({32{1'b0}}), .rem(Mod));

  // Other names for the same wires on the sheet: a_sign = A[31]; b_sign = B[31]; Signed_div[31:0] = Output_2;
  //   Unsigned_div[31:0] = Output

  // Notes on the sheet:
  //   Negate Inputs
endmodule

module Instruction_Decoder (
  input  [31:0] Instruction,
  output [4:0] Data_Address,
  output [4:0] Sa,
  output [4:0] Sb,
  output [25:0] Destino_Salto,
  output Mult_Div,
  output R_W,
  output [31:0] K,
  output Tipo_I,
  output [3:0] Selector_Alu,
  output [2:0] Selector_Branch,
  output jmp,
  output Output,
  output Output_2,
  output Output_3,
  output Output_4,
  output Output_5,
  output Output_6
);

  wire add, addi, \and , andi, beq, bgtz, blez, bltz, bne, comparator_18_eq, comparator_19_eq,
       comparator_20_eq, comparator_21_eq, comparator_22_eq, comparator_23_eq, comparator_24_eq,
       comparator_25_eq, comparator_26_eq, comparator_27_eq, comparator_28_eq, comparator_29_eq,
       comparator_30_eq, comparator_31_eq, comparator_32_eq, comparator_33_eq, comparator_34_eq,
       comparator_35_eq, comparator_36_eq, comparator_37_eq, comparator_38_eq, comparator_39_eq, div, divu,
       j, jr, lw, mfhi, mflo, mult, mulu, nop, \nor , oper, \or , or_1_out, or_2_out, or_3_out, or_4_out,
       or_5_out, or_6_out, ori, slt, slti, sltiu, sltu, special, stack, sub, sw, Tipo_R, \xor , xori;

  // Probe on Instruction[31:26]
  or or_1 (or_1_out, \and , andi);
  Comparator #(.width(6)) comparator_1 (.a(Instruction[31:26]), .b({6{1'b0}}), .eq(oper));  // open: gt, lt
  Comparator #(.width(6)) comparator_2 (.a(Instruction[31:26]), .b(6'b111000), .eq(stack));  // open: gt, lt
  Comparator #(.width(6)) comparator_3 (.a(Instruction[31:26]), .b({6{1'b1}}), .eq(special));  // open: gt, lt
  Comparator #(.width(6)) comparator_4 (.a(Instruction[31:26]), .b(6'b001000), .eq(addi));  // open: gt, lt
  Comparator #(.width(6)) comparator_5 (.a(Instruction[31:26]), .b(6'b001100), .eq(andi));  // open: gt, lt
  Comparator #(.width(6)) comparator_6 (.a(Instruction[31:26]), .b(6'b001101), .eq(ori));  // open: gt, lt
  Comparator #(.width(6)) comparator_7 (.a(Instruction[31:26]), .b(6'b001110), .eq(xori));  // open: gt, lt
  Comparator #(.width(6)) comparator_8 (.a(Instruction[31:26]), .b(6'b001010), .eq(slti));  // open: gt, lt
  Comparator #(.width(6)) comparator_9 (.a(Instruction[31:26]), .b(6'b001011), .eq(sltiu));  // open: gt, lt
  Comparator #(.width(6)) comparator_10 (.a(Instruction[31:26]), .b(6'b000100), .eq(beq));  // open: gt, lt
  Comparator #(.width(6)) comparator_11 (.a(Instruction[31:26]), .b(6'b000101), .eq(bne));  // open: gt, lt
  Comparator #(.width(6)) comparator_12 (.a(Instruction[31:26]), .b(6'b000110), .eq(blez));  // open: gt, lt
  Comparator #(.width(6)) comparator_13 (.a(Instruction[31:26]), .b(6'b000111), .eq(bgtz));  // open: gt, lt
  Comparator #(.width(6)) comparator_14 (.a(Instruction[31:26]), .b(6'b000001), .eq(bltz));  // open: gt, lt
  Comparator #(.width(6)) comparator_15 (.a(Instruction[31:26]), .b(6'b100011), .eq(lw));  // open: gt, lt
  Comparator #(.width(6)) comparator_16 (.a(Instruction[31:26]), .b(6'b101011), .eq(sw));  // open: gt, lt
  Comparator #(.width(6)) comparator_17 (.a(Instruction[31:26]), .b(6'b000010), .eq(j));  // open: gt, lt
  or or_2 (or_2_out, add, addi, lw, sw);
  or or_3 (or_3_out, \or , ori);
  or or_4 (or_4_out, \xor , xori);
  or or_5 (or_5_out, slt, slti);
  or or_6 (or_6_out, sltu, sltiu);
  or or_7 (Tipo_R, oper, stack, special);
  or or_8 (Tipo_I, addi, andi, ori, xori, slti, sltiu, beq, bne, blez, bgtz, bltz, lw, sw);
  Operation_Alu operation_alu_1 (
    .Addition(or_2_out), .Substract(sub), .Multiply(mult), .Unsigned_Multiply(mulu), .Divide(div),
    .Unsigned_Divide(divu), .Logical_And(or_1_out), .Logical_Or(or_3_out), .Logical_Nor(\nor ),
    .Logical_Xor(or_4_out), .Set_less_than(or_5_out), .Unsigned_set_less_than(or_6_out),
    .Selector_Alu(Selector_Alu), .Move_from_Hi(mfhi), .Move_from_Lo(mflo));
  // Probe on Instruction[5:0]
  Comparator #(.width(6)) comparator_18 (.a(Instruction[5:0]), .b(6'b100000), .eq(comparator_18_eq));  // open: gt, lt
  Comparator #(.width(6)) comparator_19 (.a(Instruction[5:0]), .b(6'b100010), .eq(comparator_19_eq));  // open: gt, lt
  Comparator #(.width(6)) comparator_20 (.a(Instruction[5:0]), .b(6'b011000), .eq(comparator_20_eq));  // open: gt, lt
  Comparator #(.width(6)) comparator_21 (.a(Instruction[5:0]), .b(6'b011001), .eq(comparator_21_eq));  // open: gt, lt
  Comparator #(.width(6)) comparator_22 (.a(Instruction[5:0]), .b(6'b011010), .eq(comparator_22_eq));  // open: gt, lt
  Comparator #(.width(6)) comparator_23 (.a(Instruction[5:0]), .b(6'b011011), .eq(comparator_23_eq));  // open: gt, lt
  Comparator #(.width(6)) comparator_24 (.a(Instruction[5:0]), .b(6'b100100), .eq(comparator_24_eq));  // open: gt, lt
  Comparator #(.width(6)) comparator_25 (.a(Instruction[5:0]), .b(6'b100101), .eq(comparator_25_eq));  // open: gt, lt
  Comparator #(.width(6)) comparator_26 (.a(Instruction[5:0]), .b(6'b100111), .eq(comparator_26_eq));  // open: gt, lt
  Comparator #(.width(6)) comparator_27 (.a(Instruction[5:0]), .b(6'b101000), .eq(comparator_27_eq));  // open: gt, lt
  Comparator #(.width(6)) comparator_28 (.a(Instruction[5:0]), .b(6'b101010), .eq(comparator_28_eq));  // open: gt, lt
  Comparator #(.width(6)) comparator_29 (.a(Instruction[5:0]), .b(6'b101011), .eq(comparator_29_eq));  // open: gt, lt
  Comparator #(.width(6)) comparator_30 (.a(Instruction[5:0]), .b(6'b010000), .eq(comparator_30_eq));  // open: gt, lt
  Comparator #(.width(6)) comparator_31 (.a(Instruction[5:0]), .b(6'b010010), .eq(comparator_31_eq));  // open: gt, lt
  Comparator #(.width(6)) comparator_32 (.a(Instruction[5:0]), .b({6{1'b0}}), .eq(comparator_32_eq));  // open: gt, lt
  Comparator #(.width(6)) comparator_33 (.a(Instruction[5:0]), .b(6'b001000), .eq(comparator_33_eq));  // open: gt, lt
  Comparator #(.width(6)) comparator_34 (.a(Instruction[5:0]), .b({6{1'b0}}), .eq(comparator_34_eq));  // open: gt, lt
  Comparator #(.width(6)) comparator_35 (.a(Instruction[5:0]), .b(6'b000001), .eq(comparator_35_eq));  // open: gt, lt
  Comparator #(.width(6)) comparator_36 (.a(Instruction[5:0]), .b({6{1'b1}}), .eq(comparator_36_eq));  // open: gt, lt
  Comparator #(.width(6)) comparator_37 (.a(Instruction[5:0]), .b(6'b000001), .eq(comparator_37_eq));  // open: gt, lt
  Comparator #(.width(6)) comparator_38 (.a(Instruction[5:0]), .b(6'b000010), .eq(comparator_38_eq));  // open: gt, lt
  Comparator #(.width(6)) comparator_39 (.a(Instruction[5:0]), .b(6'b000100), .eq(comparator_39_eq));  // open: gt, lt
  and and_1 (add, Tipo_R, comparator_18_eq);
  and and_2 (sub, Tipo_R, comparator_19_eq);
  and and_3 (mult, Tipo_R, comparator_20_eq);
  and and_4 (mulu, Tipo_R, comparator_21_eq);
  and and_5 (div, Tipo_R, comparator_22_eq);
  and and_6 (divu, Tipo_R, comparator_23_eq);
  and and_7 (\and , Tipo_R, comparator_24_eq);
  and and_8 (\or , Tipo_R, comparator_25_eq);
  and and_9 (\nor , Tipo_R, comparator_26_eq);
  and and_10 (\xor , Tipo_R, comparator_27_eq);
  and and_11 (slt, Tipo_R, comparator_28_eq);
  and and_12 (sltu, Tipo_R, comparator_29_eq);
  and and_13 (mfhi, Tipo_R, comparator_30_eq);
  and and_14 (mflo, Tipo_R, comparator_31_eq);
  and and_15 (nop, Tipo_R, comparator_32_eq);
  and and_16 (jr, Tipo_R, comparator_33_eq);
  and and_17 (Output, stack, comparator_34_eq);
  and and_18 (Output_2, stack, comparator_35_eq);
  and and_19 (Output_3, special, comparator_36_eq);
  and and_20 (Output_4, special, comparator_37_eq);
  and and_21 (Output_5, special, comparator_38_eq);
  and and_22 (Output_6, special, comparator_39_eq);
  Multiplexer #(.width(5), .enable("false")) multiplexer_1 (
    .in0(Instruction[25:21]), .in1(Instruction[15:11]), .out(Sa), .sel(Output_2));
  Multiplexer #(.width(5), .enable("false")) multiplexer_2 (
    .in0(Instruction[15:11]), .in1(Instruction[25:21]), .out(Sb), .sel(Output_2));
  Multiplexer #(.width(5)) multiplexer_3 (
    .in0(Instruction[10:6]), .in1(Instruction[15:11]), .out(Data_Address), .sel(Tipo_I), .en(1'b1));
  or or_9 (Mult_Div, mult, mulu, div, divu);
  assign K = {{16{1'b0}}, Instruction[15:0]};  // Bit_Extender bit_extender_1
  Branch_Jump branch_jump_1 (
    .Branch_on_equal(beq), .Branch_on_not_equal(bne), .Branch_on_less_than_or_equal_zero(blez),
    .Branch_on_greater_than_zero(bgtz), .Branch_on_less_than_zero(bltz), .Jump(j), .Jump_register(jr),
    .Branch_Selector(Selector_Branch));
  or or_10 (R_W, add, sub, \and , \or , \nor , \xor , slt, sltu, mfhi, mflo, Output, Output_5, addi, andi, ori, xori, slti, sltiu, lw);
  or or_11 (jmp, jr, j, bltz, bgtz, blez, bne, beq);

  assign Destino_Salto = Instruction[25:0];

  // Other names for the same wires on the sheet: halt = Output_3; Constante[15:0] = Instruction[15:0];
  //   Func_code[5:0] = Instruction[5:0]; Rd[4:0] = Instruction[10:6]; Rt[4:0] = Instruction[15:11];
  //   Rs[4:0] = Instruction[25:21]; Op_code[5:0] = Instruction[31:26]; Tipo_J = j; kbd = Output_6; pop = Output;
  //   push = Output_2; rnd = Output_5; tty = Output_4

  // Notes on the sheet:
  //   Formato R
  //   Formato I
  //   Instrucciones tipo R
  //   Formato J
  //   Outputs
endmodule

module Operation_Alu (
  input  Addition,
  input  Substract,
  input  Multiply,
  input  Unsigned_Multiply,
  input  Divide,
  input  Unsigned_Divide,
  input  Logical_And,
  input  Logical_Or,
  input  Logical_Nor,
  input  Logical_Xor,
  input  Set_less_than,
  input  Unsigned_set_less_than,
  input  Move_from_Hi,
  input  Move_from_Lo,
  output [3:0] Selector_Alu
);

  wire not_1_out, not_2_out, not_3_out, not_4_out, not_5_out, not_6_out, not_7_out, not_8_out, not_9_out,
       not_10_out, not_11_out, not_12_out, not_13_out, not_14_out, not_15_out, not_16_out, not_17_out,
       not_18_out, not_19_out, not_20_out, not_21_out, not_22_out, not_23_out, not_24_out, not_25_out,
       not_26_out, not_27_out, not_28_out, not_29_out, not_30_out, not_31_out;

  not not_1 (not_1_out, Addition);
  not not_2 (not_2_out, Multiply);
  not not_3 (not_3_out, Divide);
  not not_4 (not_4_out, Logical_And);
  not not_5 (not_5_out, Logical_Nor);
  not not_6 (not_6_out, Set_less_than);
  not not_7 (not_7_out, Move_from_Hi);
  not not_8 (not_8_out, Addition);
  not not_9 (not_9_out, Substract);
  not not_10 (not_10_out, Divide);
  not not_11 (not_11_out, Unsigned_Divide);
  not not_12 (not_12_out, Logical_Nor);
  not not_13 (not_13_out, Logical_Xor);
  not not_14 (not_14_out, Move_from_Hi);
  not not_15 (not_15_out, Move_from_Lo);
  and and_1 (Selector_Alu[0], not_1_out, not_2_out, not_3_out, not_4_out, not_5_out, not_6_out, not_7_out);
  and and_2 (Selector_Alu[1], not_8_out, not_9_out, not_10_out, not_11_out, not_12_out, not_13_out, not_14_out, not_15_out);
  not not_16 (not_16_out, Addition);
  not not_17 (not_17_out, Substract);
  not not_18 (not_18_out, Addition);
  not not_19 (not_19_out, Substract);
  not not_20 (not_20_out, Multiply);
  not not_21 (not_21_out, Unsigned_Multiply);
  not not_22 (not_22_out, Divide);
  not not_23 (not_23_out, Unsigned_Divide);
  not not_24 (not_24_out, Logical_And);
  not not_25 (not_25_out, Logical_Or);
  not not_26 (not_26_out, Multiply);
  not not_27 (not_27_out, Unsigned_Multiply);
  not not_28 (not_28_out, Logical_Nor);
  not not_29 (not_29_out, Logical_Xor);
  not not_30 (not_30_out, Set_less_than);
  not not_31 (not_31_out, Unsigned_set_less_than);
  and and_3 (Selector_Alu[2], not_16_out, not_17_out, not_26_out, not_27_out, not_28_out, not_29_out, not_30_out, not_31_out);
  and and_4 (Selector_Alu[3], not_18_out, not_19_out, not_20_out, not_21_out, not_22_out, not_23_out, not_24_out, not_25_out);

  // Other names for the same wires on the sheet: add = Addition; and = Logical_And; mfhi = Move_from_Hi;
  //   mflo = Move_from_Lo; nor = Logical_Nor; or = Logical_Or; Bit_1 = Selector_Alu[0]; Bit_2 = Selector_Alu[1];
  //   Bit_3 = Selector_Alu[2]; Bit_4 = Selector_Alu[3]; Signed_Div = Unsigned_Divide; Signed_Mult = Multiply;
  //   slt = Set_less_than; sltu = Unsigned_set_less_than; sub = Substract; Unsigned_Div = Divide;
  //   Unsigned_Mult = Unsigned_Multiply; xor = Logical_Xor
endmodule

module Data_Path (
  input  Kbd_Available,
  input  [6:0] Kbd_ASCII_Data,
  input  [31:0] RAM_Out_0,
  input  [3:0] Read_Time,
  input  [3:0] Write_Time,
  input  [31:0] RAM_Out_1,
  input  Reset,
  input  [31:0] RAM_Out_2,
  input  Clock,
  input  [31:0] RAM_Out_3,
  input  [31:0] in_11,
  input  [31:0] in_12,
  output Kbd_Enable,
  output [15:0] Address,
  output Kbd_Clear,
  output [3:0] Mask,
  output [31:0] RAM_In_0,
  output TTY_Enable,
  output [31:0] RAM_In_1,
  output [6:0] TTY_ASCII_Data,
  output nRead_Write,
  output Chip_Select,
  output [31:0] RAM_In_2,
  output Stop,
  output [31:0] RAM_In_3
);

  wire FC, Inmediate, j, jmp, Mult_Div, or_1_out, pop, push, Read_Write, Rnd;
  wire [2:0] Sb;
  wire [3:0] Operation;
  wire [4:0] Data_Address, Selector_A, Selector_B;
  wire [25:0] Destino_Salto;
  wire [31:0] A, adder_1_out, adder_2_out, B, Constant, IA_prime, instruction_memory_1_output,
       instruction_register_1_output_instr, JS, multiplexer_2_out, multiplier_1_out, PC, Result, SP;

  Branch_Control Branch_Control (.in_1(jmp), .in_2(FC), .in_4(JS), .Output(IA_prime), .in_3(PC));
  Branch_Operation branch_operation_1 (.Rs(A), .Rt(B), .Code(Sb), .FC(FC), .j(j));
  Adder #(.width(32)) adder_1 (.a(PC), .b(32'h4), .out(adder_1_out));  // open: cin, cout
  Multiplier #(.width(32)) multiplier_1 (.a(Constant), .b(32'h4), .out(multiplier_1_out));  // open: cin, cout
  Adder #(.width(32)) adder_2 (.a(adder_1_out), .b(multiplier_1_out), .out(adder_2_out));  // open: cin, cout
  Multiplexer #(.width(32)) multiplexer_1 (
    .in0(adder_2_out), .in1({PC[31:28], Destino_Salto, 2'b00}), .out(JS), .sel(j));  // open: en
  Register_File Register_File (
    .DA(Data_Address), .A(A), .DI(in_11), .B(B), .R_W(Read_Write), .SA(Selector_A), .SB(Selector_B),
    .Reset(Clock), .Pop(pop), .Push(push), .Clk(Clock), .Random(Rnd), .KBD(Kbd_Enable),
    .Kbd_Available(Kbd_Available), .Kbd_ASCII_Data(Kbd_ASCII_Data), .SP(SP));
  Program_Counter program_counter_1 (.Input(IA_prime), .Clock(Clock), .Output(PC), .Reset(Reset));  // open: Enable
  Multiplexer #(.width(32)) multiplexer_2 (
    .in0(B), .in1(Constant), .out(multiplexer_2_out), .sel(Inmediate));  // open: en
  Instruction_Memory instruction_memory_1 (
    .Clock(Clock), .Reset(Reset), .Instruction(in_12), .Output(instruction_memory_1_output));  // open: Enable
  ALU ALU (
    .A(A), .B(multiplexer_2_out), .R(Result), .Operation(Operation), .M_D(Mult_Div), .Push_Pop(or_1_out),
    .SP(SP));
  or or_1 (or_1_out, pop, push);
  Instruction_Register instruction_register_1 (
    .Input_Instr(instruction_memory_1_output), .Output_Instr(instruction_register_1_output_instr),
    .Clock(Clock), .Clear(Reset));  // open: Enable
  Instruction_Decoder Instruction_Decoder (
    .Instruction(instruction_register_1_output_instr), .Data_Address(Data_Address), .Sa(Selector_A),
    .Sb(Selector_B), .Destino_Salto(Destino_Salto), .Mult_Div(Mult_Div), .R_W(Read_Write), .K(Constant),
    .Selector_Alu(Operation), .Tipo_I(Inmediate), .Selector_Branch(Sb), .jmp(jmp), .Output(push),
    .Output_2(pop), .Output_3(Stop), .Output_4(TTY_Enable), .Output_5(Rnd), .Output_6(Kbd_Enable));

  // Other names for the same wires on the sheet: CLK = Clock; CLR = Reset; CS = Chip_Select;
  //   KBD_AVAIL = Kbd_Available; KBD_CLR = Kbd_Clear; KBD_DATA[6:0] = Kbd_ASCII_Data; RAM_A[15:0] = Address;
  //   RAM_INPUT_0[31:0] = RAM_In_0; RAM_INPUT_1[31:0] = RAM_In_1; RAM_INPUT_2[31:0] = RAM_In_2;
  //   RAM_INPUT_3[31:0] = RAM_In_3; RAM_MASK[3:0] = Mask; RAM_OUTPUT_0[31:0] = RAM_Out_0;
  //   RAM_OUTPUT_1[31:0] = RAM_Out_1; RAM_OUTPUT_2[31:0] = RAM_Out_2; RAM_OUTPUT_3[31:0] = RAM_Out_3;
  //   RW = nRead_Write; TTY_DATA[6:0] = TTY_ASCII_Data

  // Notes on the sheet:
  //   RAM ADDRESS
  //   DATA FROM RAM
  //   DATA TO RAM
  //   DATA WRITE MASK
  //   RAM TIMING
  //   RAM CONTROL
  //   KEYBOARD
  //   TTY
  //   SEQUENCING
endmodule

module Program_Counter (
  input  [31:0] Input,
  input  Clock,
  input  Enable,
  input  Reset,
  output [31:0] Output
);

  wire d_ff_1_q, d_ff_1_qn, kick_off;
  wire [31:0] multiplexer_1_out;

  Multiplexer #(.width(32)) multiplexer_1 (
    .in0(Input), .in1({32{1'b0}}), .out(multiplexer_1_out), .sel(kick_off));  // open: en
  D_Flip_Flop #(.trigger("falling")) d_ff_1 (
    .clk(Clock), .D(d_ff_1_qn), .Q(d_ff_1_q), .Qn(d_ff_1_qn), .en(d_ff_1_qn));  // open: preset, reset
  Register #(.width(32)) register_1 (.D(multiplexer_1_out), .en(Enable), .Q(Output), .clr(Reset));  // open: clk
  D_Flip_Flop d_ff_2 (.clk(Clock), .D(d_ff_1_q), .Qn(kick_off), .en(kick_off));  // open: Q, preset, reset

  // Other names for the same wires on the sheet: Clck = Clock; Clr = Reset; En = Enable
endmodule

module Branch_Jump (
  input  Branch_on_equal,
  input  Branch_on_not_equal,
  input  Branch_on_less_than_or_equal_zero,
  input  Branch_on_greater_than_zero,
  input  Branch_on_less_than_zero,
  input  Jump,
  input  Jump_register,
  output [2:0] Branch_Selector
);

  wire not_1_out, not_2_out, not_3_out, not_4_out, not_5_out, not_6_out, not_7_out, not_8_out, not_9_out,
       not_10_out, not_11_out, not_12_out;

  not not_1 (not_1_out, Branch_on_equal);
  not not_2 (not_2_out, Branch_on_less_than_or_equal_zero);
  not not_3 (not_3_out, Branch_on_less_than_zero);
  not not_4 (not_4_out, Jump_register);
  not not_5 (not_5_out, Branch_on_equal);
  not not_6 (not_6_out, Branch_on_not_equal);
  not not_7 (not_7_out, Branch_on_less_than_zero);
  not not_8 (not_8_out, Jump);
  not not_9 (not_9_out, Branch_on_equal);
  not not_10 (not_10_out, Branch_on_not_equal);
  not not_11 (not_11_out, Branch_on_less_than_or_equal_zero);
  not not_12 (not_12_out, Branch_on_greater_than_zero);
  and and_1 (Branch_Selector[0], not_1_out, not_2_out, not_3_out, not_4_out);
  and and_2 (Branch_Selector[1], not_5_out, not_6_out, not_7_out, not_8_out);
  and and_3 (Branch_Selector[2], not_9_out, not_10_out, not_11_out, not_12_out);

  // Other names for the same wires on the sheet: beq = Branch_on_equal; bgtz = Branch_on_greater_than_zero;
  //   blez = Branch_on_less_than_or_equal_zero; bltz = Branch_on_less_than_zero; bne = Branch_on_not_equal;
  //   bit_1 = Branch_Selector[0]; bit_2 = Branch_Selector[1]; bit_3 = Branch_Selector[2]; j = Jump;
  //   jr = Jump_register
endmodule

module Instruction_Memory (
  input  Clock,
  input  Reset,
  input  [31:0] Instruction,
  input  Enable,
  output [31:0] Output
);

  Register #(.width(32)) register_1 (
    .D(Instruction), .en(Enable), .Q({Output[7:0], Output[15:8], Output[23:16], Output[31:24]}), .clk(Clock),
    .clr(Reset));

  // Other names for the same wires on the sheet: Clk = Clock; En = Enable; Rst = Reset
endmodule

module Branch_Control (
  input  in_1,
  input  in_2,
  input  [31:0] in_3,
  input  [31:0] in_4,
  output [31:0] Output
);

  wire and_1_out;
  wire [31:0] adder_1_out, adder_2_out;

  Adder #(.width(32)) adder_1 (.a(in_3), .b(32'h4), .out(adder_1_out));  // open: cin, cout
  Adder #(.width(32)) adder_2 (.a(in_3), .b(in_4), .out(adder_2_out));  // open: cin, cout
  Multiplexer #(.width(32)) multiplexer_1 (
    .in0(adder_1_out), .in1(adder_2_out), .out(Output), .sel(and_1_out));  // open: en
  and and_1 (and_1_out, in_2, in_1);

  // Other names for the same wires on the sheet: FC = in_2; IA[31:0] = in_3; jmp = in_1; JS[31:0] = in_4
endmodule

// Br Op
module Branch_Operation (
  input  [31:0] Rs,
  input  [31:0] Rt,
  input  [2:0] Code,
  output FC,
  output j
);

  wire beq, bgtz, blez, bltz, bne, comparator_2_eq, decoder_1_out0, decoder_1_out1, decoder_1_out2,
       decoder_1_out3, decoder_1_out4;

  Decoder #(.select(3), .enable("false")) decoder_1 (
    .out0(decoder_1_out0), .out1(decoder_1_out1), .out2(decoder_1_out2), .out3(decoder_1_out3),
    .out4(decoder_1_out4), .out5(j), .sel(Code));  // open: out6, out7
  Comparator #(.width(32)) comparator_1 (.a(Rs), .b(Rt), .eq(beq));  // open: gt, lt
  not not_1 (bne, beq);
  Comparator #(.width(32)) comparator_2 (.a(Rs), .b({32{1'b0}}), .gt(bgtz), .eq(comparator_2_eq), .lt(bltz));
  or or_1 (blez, comparator_2_eq, bltz);
  Branch_Selector branch_selector_1 (
    .Op_beq(decoder_1_out0), .Cond_beq(beq), .Op_bne(decoder_1_out1), .Cond_bne(bne),
    .Op_blez(decoder_1_out2), .Cond_blez(blez), .Op_bgtz(decoder_1_out3), .Cond_bgtz(bgtz),
    .Op_bltz(decoder_1_out4), .Cond_bltz(bltz), .Flag_Condition(FC));
endmodule

module Branch_Selector (
  input  Op_beq,
  input  Cond_beq,
  input  Op_bne,
  input  Cond_bne,
  input  Op_blez,
  input  Cond_blez,
  input  Op_bgtz,
  input  Cond_bgtz,
  input  Op_bltz,
  input  Cond_bltz,
  output Flag_Condition
);

  wire and_1_out, and_2_out, and_3_out, and_4_out, and_5_out;

  and and_1 (and_1_out, Op_beq, Cond_beq);
  and and_2 (and_2_out, Op_bne, Cond_bne);
  and and_3 (and_3_out, Op_blez, Cond_blez);
  and and_4 (and_4_out, Op_bgtz, Cond_bgtz);
  and and_5 (and_5_out, Op_bltz, Cond_bltz);
  or or_1 (Flag_Condition, and_1_out, and_2_out, and_3_out, and_4_out, and_5_out);
endmodule

module Instruction_Register (
  input  [31:0] Input_Instr,
  input  Enable,
  input  Clock,
  input  Clear,
  output [31:0] Output_Instr
);

  Register #(.width(32)) register_1 (.D(Input_Instr), .en(Enable), .Q(Output_Instr), .clk(Clock), .clr(Clear));
endmodule
